# Fritzing sketch manusa_licenta (saved by Fritzing 1.0.4)
breadboards: 1

parts:
  U1 = ESP32-38PinWide [part_number=ESP32-38PinWide]
  Adafruit_PCA9546_4-Channel_I2C_Multiplexer1 = Adafruit PCA9546 4-Channel I2C Multiplexer [part_number=#5663]
  LED1 = RGB LED - (4 legs) [color="Red (633nm)" current=0.030A package="5 mm [THT]"]
  R1 = Basic Flex Resistor
  R2 = Basic Flex Resistor
  R3 = Basic Flex Resistor
  Part1 = InvenSense MPU6050
  Part2 = InvenSense MPU6050
  Part3 = InvenSense MPU6050
  R4 = Resistor [tolerance=±5% resistance=220 package="0402 [SMD]"]
  R5 = Resistor [tolerance=±5% resistance=220 package="0402 [SMD]"]
  R6 = Resistor [tolerance=±5% resistance=220 package="0402 [SMD]"]
  R7 = Resistor [tolerance=±5% resistance=220 package="0402 [SMD]"]
  R8 = Resistor [tolerance=±5% resistance=220 package="0402 [SMD]"]
  R9 = Resistor [tolerance=±5% resistance=220 package="0402 [SMD]"]
  J1 = Piezo Speaker

nets:
  VCC: U1.3.3, Part1.VCC, Part2.VCC, Part3.VCC, R4.Pin_0, R5.Pin_1, R6.Pin_1
  GND: U1.GND, LED1.common_anode, R1.Pin_1, R2.Pin_1, R3.Pin_1, Part1.GND, Part2.GND, Part3.GND, J1.pin1
  N1: U1.GPIO15, R3.Pin_2, R4.Pin_1
  N2: U1.GPIO2, R2.Pin_2, R5.Pin_0
  N3: U1.GPIO4, R1.Pin_2, R6.Pin_0
  N4: U1.GPIO16, J1.pin2
  N5: U1.GPIO5, R8.Pin_0
  N6: U1.GPIO18, R7.Pin_0
  N7: U1.GPIO21, Adafruit_PCA9546_4-Channel_I2C_Multiplexer1.INPUTSCL
  N8: U1.GPIO22, Adafruit_PCA9546_4-Channel_I2C_Multiplexer1.INPUTSDA
  N9: Adafruit_PCA9546_4-Channel_I2C_Multiplexer1.2SCL, Part2.SCL
  N10: Adafruit_PCA9546_4-Channel_I2C_Multiplexer1.2SDA, Part2.SDA
  N11: Adafruit_PCA9546_4-Channel_I2C_Multiplexer1.1SCL, Part3.SCL
  N12: Adafruit_PCA9546_4-Channel_I2C_Multiplexer1.1SDA, Part3.SDA
  N13: Adafruit_PCA9546_4-Channel_I2C_Multiplexer1.0SCL, Part1.SCL
  N14: Adafruit_PCA9546_4-Channel_I2C_Multiplexer1.0SDA, Part1.SDA
  N15: LED1.red_cathode, R9.Pin_1
  N16: LED1.green_cathode, R8.Pin_1
  N17: LED1.blue_cathode, R7.Pin_1

custom parts:
  ESP32-38PinWide: Generic 38-Pin ESP32 with wide format (only access to one side of pins on a breadboard) based on Stephen Lilley's HiLetgo ESP-WROOM-32 ESP32 ESP-32S Development Board.
  Adafruit PCA9546 4-Channel I2C Multiplexer: You just found the perfect I2C sensor, and you want to wire up two or three or more of them to your Arduino when you realize "Uh oh, this chip has a fixed I2C address, and from what I know about I2C, you cannot have two devices with the same address on the same SDA/SCL pins!" Are you out of luck? You would be if you didn't have this ultra-cool PCA9546 1-to-4 I2C multiplexer! Finally, a way to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
